# Fritzing sketch schema (saved by Fritzing 0.9.5d)

parts:
  RGB_Strip_LED1 = RGB Strip LED
  Componente1 = Arduino Uno (Rev3)

nets:
  N1: RGB_Strip_LED1.Common_Connect#4, Componente1.5V
  N2: RGB_Strip_LED1.Blue_Connect#5, Componente1.D5_PWM
  N3: RGB_Strip_LED1.Red_Connect#6, Componente1.D6_PWM
  N4: RGB_Strip_LED1.Green_Connect#7, Componente1.D9_PWM

custom parts:
  RGB Strip LED: A tri-color Strip LED with red, green and blue. Pin order: red - common cathode - blue - green
